# Fritzing sketch wiring (saved by Fritzing 0.8.7b)
breadboards: 1

parts:
  Raspberry_Pi_1 = Raspberry Pi 3
  R1 = Resistor [tolerance=±5% resistance=1.5k package=THT]
  R2 = Resistor [tolerance=±5% resistance=2.2k package=THT]
  R3 = Resistor [tolerance=±5% resistance=1.5k package=THT]
  R4 = Resistor [tolerance=±5% resistance=2.2k package=THT]

nets:
  N1: Raspberry_Pi_1.GND, R2.Pin_1, R4.Pin_1
  N2: Raspberry_Pi_1.GIPO15, R3.Pin_0, R4.Pin_0
  N3: Raspberry_Pi_1.GIPO14, R1.Pin_0, R2.Pin_0

notes:
  X signal
  Y signal
  Z signal
  4 signal
  X1 signal
  X10 signal
  X100 signal
  EStop signal
  LED+ signal
  LED- signal
  5V
  A signal
  B signal
  1200Ω
  0V
  COM
  EStop signal return
  2200Ω
